# Fritzing sketch hidden_device (saved by Fritzing 1.0.0rc)
breadboards: 1

parts:
  part = Arduino Uno Mini LE
  FSR = Basic Force Sensing Resistor (FSR) [package=THT]
  R1 = Resistor [tolerance=±5% power=0.25W resistance=10k part_number=. package=THT]
  U1 = ESP8266 ESP-01 Upgraded WiFi Module [part_number=.]
  R2 = Resistor [tolerance=±5% power=0.25W resistance=10k package=THT]
  R3 = Resistor [tolerance=±5% power=0.25W resistance=10k package=THT]
  R4 = Resistor [tolerance=±5% power=0.25W resistance=10k package=THT]
  Buzzer = Piezo Speaker
  part_2 = Resistor [tolerance=±5% power=0.25W resistance=220 package=THT]
  part_3 = KY-019 5V Relay Module [package="Breakout board"]
  part_4 = Battery block 9V

nets:
  N1: part.A0, FSR.pin_1, R1.Pin_0
  N2: part.D9_PWM, part_3.S
  N3: part.D11_PWM/MOSI, part_2.Pin_0
  GND: part.GND, R1.Pin_1, U1.GND, R2.Pin_0, Buzzer.pin1, part_3.-
  N4: part.D3_PWM, U1.TXD
  N5: part.D5_PWM, R4.Pin_1
  N6: part.D7, part.RESET
  3V3: part.3V3, FSR.pin_2, U1.VCC, U1.CH_PD, part_3.+
  N7: U1.RXD, R3.Pin_1, R4.Pin_0
  N8: R2.Pin_1, R3.Pin_0
  N9: Buzzer.pin2, part_2.Pin_1
  N10: part_3.Common, part_4.+

custom parts:
  Arduino Uno Mini LE: The UNO Mini Limited Edition (LE) is a miniature version of the classic Arduino UNO board. It is based on the ATmega328P microcontroller, has USB-C connector for programming and powering the board, and pins available for connecting external power sources. It also comes with the standard set of female pin connectors, built-in LED, reset button and everything else that the standard UNO have, but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
  ESP8266 ESP-01 Upgraded WiFi Module: Upgraded Version ESP-01,all Flash are upgraded to 1M byte.Also support Cloud service remote transmission.
  KY-019 5V Relay Module: KY-019 5V Relay module, used to control AC circuits. (Special thanks to vanepp for fixing the PCB holes and other errors)
